// Logisim project imm-gen.circ as structural Verilog: 1 circuit, main circuit imm_gen
module imm_gen (
  input  [31:0] Instruction,
  input  [2:0] ImmSel,
  output [31:0] Immediate
);

  wire [31:0] B, I, IStar, J, multiplexer_1_out, NewI, S;

  assign I = {{20{Instruction[31]}}, Instruction[31:20]};  // Bit_Extender bit_extender_1
  assign IStar = {{27{1'b0}}, Instruction[24:20]};  // Bit_Extender bit_extender_2
  assign S = {{20{Instruction[31]}}, {Instruction[31:25], Instruction[11:7]}};  // Bit_Extender bit_extender_3
  Multiplexer #(.select(3), .width(32)) multiplexer_1 (
    .in0(I), .in1(IStar), .in2(I), .in4(I), .in5(IStar), .in6(I), .in7(I), .out(multiplexer_1_out),
    .sel(Instruction[14:12]));  // open: in3
  assign B = {{19{Instruction[31]}}, {Instruction[31], Instruction[7], Instruction[30:25], Instruction[11:8], 1'b0}};  // Bit_Extender bit_extender_4
  assign J = {{11{Instruction[31]}}, {Instruction[31], Instruction[19:12], Instruction[20], Instruction[30:21], 1'b0}};  // Bit_Extender bit_extender_5
  Multiplexer #(.select(2), .width(32)) multiplexer_2 (
    .in0(I), .in1(multiplexer_1_out), .in2(I), .in3(I), .out(NewI), .sel(Instruction[5:4]));
  Multiplexer #(.select(3), .width(32)) multiplexer_3 (
    .in0(NewI), .in1(S), .in2(B), .in3({Instruction[31:12], {12{1'b0}}}), .in4(J), .out(Immediate),
    .sel(ImmSel));  // open: in5, in6, in7

  // Other names for the same wires on the sheet: rs2[4:0] = Instruction[24:20]; U[31:12] = Instruction[31:12];
  //   funct3[2:0] = Instruction[14:12]; rs1[4:0] = Instruction[19:15]; rd[4:0] = Instruction[11:7];
  //   funct7[6:0] = Instruction[31:25]; Opcode[6:0] = Instruction[6:0]

  // Notes on the sheet:
  //   I:
  //   I*:
  //   S:
  //   B:
  //   U:
  //   J:
  //   INPUTS to your circuit
  //   I-MUX
  //   DON'T CHANGE THE LOCATIONS OF THE INPUTS AND OUTPUTS!
  //   OUTPUT from your circuit
endmodule
