// Logisim project partial-load.circ as structural Verilog: 1 circuit, main circuit partial_load
module partial_load (
  input  [31:0] Instruction,
  input  [31:0] MemAddress,
  input  [31:0] DataFromMem,
  output [31:0] DataToReg
);

  wire is_lb, is_lh, is_lw;
  wire [1:0] BottomBits, LoadSel;
  wire [31:0] bit_extender_2_out, bit_extender_3_out, bit_extender_4_out, bit_extender_5_out,
       bit_extender_6_out, bit_extender_7_out, bit_extender_8_out, lb, lh;

  Comparator #(.width(3)) comparator_1 (.a(Instruction[14:12]), .b(3'b000), .eq(is_lb));  // open: gt, lt
  Comparator #(.width(3)) comparator_2 (.a(Instruction[14:12]), .b(3'b001), .eq(is_lh));  // open: gt, lt
  Comparator #(.width(3)) comparator_3 (.a(Instruction[14:12]), .b(3'b010), .eq(is_lw));  // open: gt, lt
  Priority_Encoder #(.select_enc(2)) priority_encoder_1 (
    .in0(is_lb), .in1(is_lh), .in2(is_lw), .out(LoadSel));  // open: in3, gs, en_out, en_in
  Bit_Extender #(.in_width(32), .out_width(2)) bit_extender_1 (.in(MemAddress), .out(BottomBits));
  assign bit_extender_2_out = {{24{DataFromMem[7]}}, DataFromMem[7:0]};  // Bit_Extender bit_extender_2
  assign bit_extender_3_out = {{24{DataFromMem[15]}}, DataFromMem[15:8]};  // Bit_Extender bit_extender_3
  assign bit_extender_4_out = {{24{DataFromMem[23]}}, DataFromMem[23:16]};  // Bit_Extender bit_extender_4
  assign bit_extender_5_out = {{24{DataFromMem[31]}}, DataFromMem[31:24]};  // Bit_Extender bit_extender_5
  assign bit_extender_6_out = {{16{DataFromMem[15]}}, DataFromMem[15:0]};  // Bit_Extender bit_extender_6
  assign bit_extender_7_out = {{16{DataFromMem[23]}}, DataFromMem[23:8]};  // Bit_Extender bit_extender_7
  assign bit_extender_8_out = {{16{DataFromMem[31]}}, DataFromMem[31:16]};  // Bit_Extender bit_extender_8
  Multiplexer #(.select(2), .width(32)) multiplexer_1 (
    .in0(bit_extender_2_out), .in1(bit_extender_3_out), .in2(bit_extender_4_out), .in3(bit_extender_5_out),
    .out(lb), .sel(BottomBits));
  Multiplexer #(.select(2), .width(32)) multiplexer_2 (
    .in0(bit_extender_6_out), .in1(bit_extender_7_out), .in2(bit_extender_8_out), .out(lh), .sel(BottomBits));  // open: in3
  Multiplexer #(.select(2), .width(32)) multiplexer_3 (
    .in0(lb), .in1(lh), .in2(DataFromMem), .out(DataToReg), .sel(LoadSel));  // open: in3

  // Other names for the same wires on the sheet: funct3[2:0] = Instruction[14:12]; lw[31:0] = DataFromMem

  // Notes on the sheet:
  //   INPUTS to your circuit
  //   DON'T CHANGE THE LOCATIONS OF THE INPUTS AND OUTPUTS!
  //   OUTPUT from your circuit
endmodule
