// Logisim project partial-store.circ as structural Verilog: 1 circuit, main circuit partial_store
module partial_store (
  input  [31:0] Instruction,
  input  [31:0] MemAddress,
  input  [31:0] DataFromReg,
  input  MemWEn,
  output [3:0] MemWriteMask,
  output [31:0] DataToMem
);

  wire and_1_out, and_2_out, and_3_out, and_4_out, and_5_out, and_6_out, and_7_out, comparator_1_eq,
       comparator_2_eq, comparator_3_eq, comparator_4_eq, comparator_5_eq, comparator_6_eq, comparator_7_eq,
       is_sb, is_sh, is_sw;
  wire [1:0] BottomBits;
  wire [3:0] bit_extender_2_out, TempMask;

  Comparator #(.width(2)) comparator_1 (.a(BottomBits), .b(2'b00), .eq(comparator_1_eq));  // open: gt, lt
  Comparator #(.width(2)) comparator_2 (.a(BottomBits), .b(2'b01), .eq(comparator_2_eq));  // open: gt, lt
  Comparator #(.width(2)) comparator_3 (.a(BottomBits), .b(2'b00), .eq(comparator_3_eq));  // open: gt, lt
  Comparator #(.width(2)) comparator_4 (.a(BottomBits), .b(2'b10), .eq(comparator_4_eq));  // open: gt, lt
  Comparator #(.width(2)) comparator_5 (.a(BottomBits), .b(2'b11), .eq(comparator_5_eq));  // open: gt, lt
  Comparator #(.width(2)) comparator_6 (.a(BottomBits), .b(2'b10), .eq(comparator_6_eq));  // open: gt, lt
  Comparator #(.width(2)) comparator_7 (.a(BottomBits), .b(2'b00), .eq(comparator_7_eq));  // open: gt, lt
  Bit_Extender #(.in_width(32), .out_width(2)) bit_extender_1 (.in(MemAddress), .out(BottomBits));
  Comparator #(.width(3)) comparator_8 (.a(Instruction[14:12]), .b(3'b000), .eq(is_sb));  // open: gt, lt
  Comparator #(.width(3)) comparator_9 (.a(Instruction[14:12]), .b(3'b001), .eq(is_sh));  // open: gt, lt
  Comparator #(.width(3)) comparator_10 (.a(Instruction[14:12]), .b(3'b010), .eq(is_sw));  // open: gt, lt
  and and_1 (and_1_out, is_sb, comparator_1_eq);
  and and_2 (and_2_out, is_sb, comparator_2_eq);
  and and_3 (and_3_out, is_sh, comparator_3_eq);
  and and_4 (and_4_out, is_sb, comparator_4_eq);
  and and_5 (and_5_out, is_sb, comparator_5_eq);
  and and_6 (and_6_out, is_sh, comparator_6_eq);
  and and_7 (and_7_out, is_sw, comparator_7_eq);
  assign bit_extender_2_out = {{3{1'b0}}, MemWEn};  // Bit_Extender bit_extender_2
  Priority_Encoder #(.select_enc(4)) priority_encoder_1 (
    .in1(and_1_out), .in2(and_2_out), .in3(and_3_out), .in4(and_4_out), .in8(and_5_out), .in12(and_6_out),
    .in15(and_7_out), .out(TempMask));  // open: in0, in5, in6, in7, in9, in10, in11, in13, in14, gs, en_out, en_in
  Multiplexer #(.width(4)) multiplexer_1 (.in0(bit_extender_2_out), .in1(TempMask), .out(MemWriteMask), .sel(MemWEn));
  Multiplexer #(.select(4), .width(32)) multiplexer_2 (
    .in0({32{1'b0}}), .in1({{24{1'b0}}, DataFromReg[7:0]}), .in2({{16{1'b0}}, DataFromReg[7:0], {8{1'b0}}}),
    .in3({{16{1'b0}}, DataFromReg[15:0]}), .in4({{8{1'b0}}, DataFromReg[7:0], {16{1'b0}}}),
    .in8({DataFromReg[7:0], {24{1'b0}}}), .in12({DataFromReg[15:0], {16{1'b0}}}), .in15(DataFromReg),
    .out(DataToMem), .sel(MemWriteMask));  // open: in5, in6, in7, in9, in10, in11, in13, in14

  // Other names for the same wires on the sheet: funct3[2:0] = Instruction[14:12]; sb0[7:0] = DataFromReg[7:0];
  //   sb1[15:8] = DataFromReg[7:0]; sb2[23:16] = DataFromReg[7:0]; sb3[31:24] = DataFromReg[7:0];
  //   sh0[15:0] = DataFromReg[15:0]; sh2[31:16] = DataFromReg[15:0]; sw0[31:0] = DataFromReg

  // Notes on the sheet:
  //   INPUTS to your circuit
  //   DON'T CHANGE THE LOCATIONS OF THE INPUTS AND OUTPUTS!
  //   OUTPUT from your circuit
endmodule
